# Fritzing sketch Arcade Schematic (saved by Fritzing 0.9.0b)
breadboards: 1

parts:
  Teensy++1 = Teensy++ 2.0
  SW1 = DIP SWITCH [package=dipswitch-02]
  SW2 = DIP SWITCH [package=dipswitch-02]
  S1 = Round Pushbutton
  S3 = Round Pushbutton
  S4 = Round Pushbutton
  S5 = Round Pushbutton
  S6 = Round Pushbutton
  S7 = Round Pushbutton
  S8 = Round Pushbutton
  S9 = Momentary Switch [package=ksa_sealed_tac_switch]
  S10 = Momentary Switch [package=ksa_sealed_tac_switch]
  S11 = Momentary Switch [package=ksa_sealed_tac_switch]
  S12 = Momentary Switch [package=ksa_sealed_tac_switch]
  S13 = Round Pushbutton
  S14 = Round Pushbutton
  Raspberry_Pi1 = Raspberry Pi B rev2  # not connected
  JP1 = RCA [package=rca_lock]  # not connected
  JP2 = RCA [package=rca_lock]  # not connected
  JP3 = RCA [package=rca_lock]  # not connected

nets:
  N1: Teensy++1.GND#0, Teensy++1.GND#21, S1.leg1, S3.leg1, S4.leg1, S5.leg1, S6.leg1, S7.leg1, S8.leg1, S9.2, S10.2, S11.2, S12.2, S13.leg1, S14.leg1
  N2: Teensy++1.D1, S8.leg0
  N3: Teensy++1.D3, S5.leg0
  N4: Teensy++1.D4, S6.leg0
  N5: Teensy++1.D5, S13.leg0
  N6: Teensy++1.D7, S14.leg0
  N7: Teensy++1.E0, SW2.3
  N8: Teensy++1.E1, SW2.4
  N9: Teensy++1.C0, SW1.3
  N10: Teensy++1.C1, SW1.4
  N11: Teensy++1.C3, S12.1
  N12: Teensy++1.C4, S9.1
  N13: Teensy++1.C5, S11.1
  N14: Teensy++1.C6, S10.1
  N15: Teensy++1.C7, S7.leg0
  N16: Teensy++1.GND#32, SW1.1, SW1.2, SW2.1, SW2.2
  N17: Teensy++1.B0, S1.leg0
  N18: Teensy++1.B1, S3.leg0
  N19: Teensy++1.B2, S4.leg0

notes:
  Joy Stick]
